# Fritzing sketch GeigerCounter (saved by Fritzing 0.9.4)
breadboards: 1

parts:
  WeMos_D1_Mini1 = WeMos D1 Mini  # not connected
  Q4 = NPN-Transistor [package="TO92 [THT]"]
  C1 = Ceramic Capacitor [capacitance=1nF package="100 mil [THT, multilayer]"]
  R1 = Resistor [tolerance=±5% resistance=4.7k package="2512 [SMD]"]
  R2 = Resistor [tolerance=±5% resistance=4.7k package="2512 [SMD]"]
  IC1 = IC, SIP package, 3 pins [chip_label=Cnt]
  IC2 = IC, SIP package, 5 pins [chip_label=Display]

nets:
  N1: Q4.E, R2.Pin_0
  N2: Q4.B, C1.0, R1.Pin_1
  N3: Q4.C, IC1.pin1
  N4: C1.1, IC1.pin3
  N5: R1.Pin_0, IC2.pin1

notes:
  NPN Mosfet S G D
  5V Rail
  3.3V Rail
