# Fritzing sketch RandomNoise (saved by Fritzing 0.9.4)
breadboards: 1

parts:
  Q1 = NPN-Transistor [package="TO92 [THT]"]
  C1 = Ceramic Capacitor [capacitance=47nF package="100 mil [THT, multilayer]"]
  R1 = Resistor [tolerance=±5% resistance=100k package=THT]
  LM1 = LM393 [chip_label=?]
  R2 = Resistor [tolerance=±5% resistance=100k package=THT]
  R3 = Resistor [tolerance=±5% resistance=100k package=THT]
  40106 = CD40106 [chip_label=CD40106 package="DIP (Dual Inline) [THT]"]
  40106_A = CD40106 [package="DIP (Dual Inline) [THT]"]  # not connected
  40106_B = CD40106 [package="DIP (Dual Inline) [THT]"]  # not connected
  40106_C = CD40106 [package="DIP (Dual Inline) [THT]"]  # not connected
  40106_D = CD40106 [package="DIP (Dual Inline) [THT]"]  # not connected
  40106_E = CD40106 [package="DIP (Dual Inline) [THT]"]  # not connected
  40106_F = CD40106 [package="DIP (Dual Inline) [THT]"]  # not connected
  40106_PWR = CD40106 [package="DIP (Dual Inline) [THT]"]  # not connected
  40106_F_2 = CD40106 [package="DIP (Dual Inline) [THT]"]  # not connected
  40106_E_2 = CD40106 [package="DIP (Dual Inline) [THT]"]  # not connected
  40106_PWR_2 = CD40106 [package="DIP (Dual Inline) [THT]"]  # not connected
  40106_D_2 = CD40106 [package="DIP (Dual Inline) [THT]"]  # not connected
  40106_C_2 = CD40106 [package="DIP (Dual Inline) [THT]"]  # not connected
  40106_2 = CD40106 [chip_label=74HC74 package="DIP (Dual Inline) [THT]"]
  40106_B_2 = CD40106 [package="DIP (Dual Inline) [THT]"]  # not connected
  40106_A_2 = CD40106 [package="DIP (Dual Inline) [THT]"]  # not connected

nets:
  N1: Q1.B, C1.0, R1.Pin_1
  N2: C1.1, LM1.In_1_+, R3.Pin_0
  N3: R1.Pin_0, LM1.In_1_-, LM1.GND, R3.Pin_1, 40106.connector6
  N4: LM1.Output_1, R2.Pin_1, 40106.connector0
  N5: LM1.VCC, 40106.connector13, 40106_2.connector6, 40106_2.connector13
  N6: 40106.connector1, 40106.connector2
  N7: 40106.connector3, 40106_2.connector2
  N8: 40106_2.connector1, 40106_2.connector5

notes:
  9V
  5V
  (N)
  (C)
  (D)
  (Dout)

custom parts:
  CD40106: Hex Inverting Schmitt Trigger
  CD40106: Hex Inverting Schmitt Trigger
  CD40106: Hex Inverting Schmitt Trigger
  CD40106: Hex Inverting Schmitt Trigger
  CD40106: Hex Inverting Schmitt Trigger
  CD40106: Hex Inverting Schmitt Trigger
  CD40106: Hex Inverting Schmitt Trigger
  CD40106: Hex Inverting Schmitt Trigger
