# Fritzing sketch SerialBridge (saved by Fritzing 0.9.4)
breadboards: 1

parts:
  Part1 = Adafruit HUZZAH32 ESP32 Feather [part_number="Adafruit #3405"]
  Part2 = Arduino Mega 2560 (Rev3)
  Part3 = TXB0104 4-channel Bi-Directional Level Shifter
  S2 = Momentary Switch [package=ksa_sealed_tac_switch]
  LED1 = Billie the Blue LED
  R1 = Resistor [tolerance=±5% resistance=330 package=THT]

nets:
  N1: Part1.IO17, Part3.A2
  N2: Part1.IO16, Part3.A1
  N3: Part1.N/C, Part3.OE
  N4: Part1.3.3V, Part3.LV
  N5: Part2.D17_PWM/RX2, Part3.B2
  N6: Part2.D16_PWM/TX2, Part3.B1
  N7: Part2.5V, Part3.HV
  GND: Part2.GND, Part3.GND, S2.1, R1.Pin_0
  N8: Part2.D2_PWM, LED1.cathode
  N9: Part2.D3_PWM, S2.3
  N10: LED1.anode, R1.Pin_1

notes:
  3.3V Rail
  5V Rail

custom parts:
  TXB0104 4-channel Bi-Directional Level Shifter: Because the Arduino (and Basic Stamp) are 5V devices, and most modern sensors, displays, flash cards and modes are 3.3V-only, many makers find that they need to perform level shifting/conversion to protect the 3.3V device from 5V. Although one can use resistors to make a divider, for high speed transfers, the resistors can add a lot of slew and cause havoc that is tough to debug. For that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
